# Fritzing sketch am312 (saved by Fritzing 1.0.6)
breadboards: 1

parts:
  A1 = Esp32-c3 super mini  # not connected
  A2 = am312 pir sensor [package=THT]
  R1 = Resistor [tolerance=±5% resistance=10k package="0805 [SMD]"]

nets:
  N1: A2.pin2, R1.Pin_1
  N2: A2.pin3, R1.Pin_0

notes:
  10kΩ

custom parts:
  Esp32-c3 super mini: ESP32-C3 Development Board ESP32 SuperMini Development Board ESP32 Development Board WiFi Bluetooth.
  am312 pir sensor: The AM312 is an ultra-miniature PIR module which uses a pyroelectric sensor similar to the one found in the common SR501 but in a more compact form factor.
