# Fritzing sketch ds18b20 (saved by Fritzing 1.0.6)
breadboards: 1

parts:
  A1 = Esp32-c3 super mini
  DS1 = DS18B20 1-Wire Temperature Sensor [part_number=DS18B20]
  R1 = Resistor [tolerance=±5% resistance=4.7k package="0805 [SMD]"]

nets:
  N1: A1.Pin_5, A1.Pin_10
  N2: A1.Pin_16, DS1.VDD, R1.Pin_0
  N3: DS1.DQ, R1.Pin_1

notes:
  4.7kΩ

custom parts:
  Esp32-c3 super mini: ESP32-C3 Development Board ESP32 SuperMini Development Board ESP32 Development Board WiFi Bluetooth.
